# Fritzing sketch final 회로도 (saved by Fritzing 0.9.3b)
breadboards: 1

parts:
  부품1 = Arduino Uno (Rev3)
  gyro_IMU_9DOF_v2_0 = 9 Degrees of Freedom - Sensor Stick
  LCD_monitor = LCD screen
  Piezo_Speaker = Piezo Speaker
  GPS = SUP500F [package=sup500f]

nets:
  N1: 부품1.A4/SDA, gyro_IMU_9DOF_v2_0.SDA, LCD_monitor.R/W
  N2: 부품1.A5/SCL, gyro_IMU_9DOF_v2_0.SCL, LCD_monitor.RS
  N3: 부품1.D8, Piezo_Speaker.pin2
  N4: 부품1.D5_PWM, GPS.TX-O
  N5: 부품1.D6_PWM, GPS.RX-I
  VCC: 부품1.5V, gyro_IMU_9DOF_v2_0.VCC, LCD_monitor.VDD, GPS.VCC
  GND: 부품1.GND, gyro_IMU_9DOF_v2_0.GND, LCD_monitor.V0, Piezo_Speaker.pin1, GPS.GND
