# Fritzing sketch final (saved by Fritzing 0.9.3b)
breadboards: 1

parts:
  부품1 = Arduino Uno (Rev3)
  Piezo_Speaker = Piezo Speaker
  GPS = SUP500F [package=sup500f]
  J1 = Basic Force Sensing Resistor (FSR) [package=THT]
  U1 = ESP8266 WiFi Module [part_number=ESP8266]
  R1 = Resistor [tolerance=±5% resistance=10k package=THT]
  부품2 = Tri-Axis Gyro Breakout - L3G4200D
  R2 = Resistor [tolerance=±5% resistance=10k package=THT]
  LED2 = smd LED [color="Red (633nm)" package="0805 [SMD]"]

nets:
  N1: 부품1.A0, J1.pin_0, R1.Pin_1
  N2: 부품1.A4/SDA, 부품2.SDA
  N3: 부품1.A5/SCL, 부품2.SCL
  N4: 부품1.D8, Piezo_Speaker.pin2
  N5: 부품1.D9_PWM, R2.Pin_0
  N6: 부품1.D1/TX, U1.GPIO_5
  N7: 부품1.D2, 부품2.INT2
  N8: 부품1.D5_PWM, GPS.TX-O
  N9: 부품1.D6_PWM, GPS.RX-I
  VCC: 부품1.5V, GPS.VCC, J1.pin_1, U1.VCC, 부품2.VCC
  GND: 부품1.GND, Piezo_Speaker.pin1, GPS.GND, U1.GND, R1.Pin_0, 부품2.GND, LED2.cathode
  N10: R2.Pin_1, LED2.anode
